// Digital circuit CPU.dig as structural Verilog
module CPU (
  input  [15:0] value,
  input  [1:0] dest,
  input  [1:0] src,
  output [15:0] r0,
  output [15:0] r1,
  output [15:0] r2,
  output [15:0] r3,
  output [15:0] B,
  output [1:0] rd,
  output [15:0] value_2,
  output [1:0] rs,
  output [15:0] value_3,
  output [3:0] PC
);

  wire add, add_out, Advance_out, assembler_1_p8, jump, jump_out, mode_out, pm_1_p6, pm_1_p7, pm_1_p8;
  wire [3:0] pm_1_p4;
  wire [15:0] execute_1_result;
  wire [31:0] assembler_1_p7, fecthc_counter_1_instr_0, pm_1_p5, PROGRAM_d;

  LED programming (.in(mode_out));
  DipSwitch mode (.out(mode_out));
  Button u_add (.out(add_out));
  Button u_jump (.out(jump_out));
  // assembler assembler_1: pin names not known; wires that end beside it: mode_out, value, dest, src, add_out, jump_out, assembler_1_p7, assembler_1_p8
  // PM pm_1: pin names not known; wires that end beside it: assembler_1_p7, assembler_1_p8, PC, pm_1_p4, pm_1_p5, pm_1_p6, pm_1_p7, pm_1_p8
  EEPROMDualPort #(.AddrBits(4), .Bits(32)) PROGRAM (
    .A(pm_1_p4), .Din(pm_1_p5), .str(pm_1_p6), .C(pm_1_p7), .ld(pm_1_p8), .D(PROGRAM_d));
  fecthc_counter fecthc_counter_1 (
    .prog(mode_out), .bypass(assembler_1_p7), .instr_i(PROGRAM_d), .clock(Advance_out), .value(value_2),
    .jump(jump), .instr_0(fecthc_counter_1_instr_0), .PC(PC));
  Button Advance (.out(Advance_out));
  LED led_1 (.in(add));
  LED led_2 (.in(jump));
  // decoder decoder_1: pin names not known; wires that end beside it: fecthc_counter_1_instr_0, value_2, rs, rd, add, jump
  execute execute_1 (.value(value_2), .B(B), .add(add), .result(execute_1_result));
  reg_file reg_file_1 (
    .RS(rs), .rd(rd), .result(execute_1_result), .clock(Advance_out), .rsval(B));  // open: rdval, R0, R1, R2, R3

  assign value_3 = value_2;

  // Other names for the same wires on the sheet: value_t[15:0] = value_2

  // Notes on the sheet:
  //   value: default 1
  //   dest: default 1
  //   src: default 1
  //   contents of PROGRAM (hex, n*v repeats v):
  //   64,1000c8,1200c8,230022,30002a,7000002
  //   pc =
  //   =
  //   +
  //   (
  //   R
  //   )
endmodule
